// Digital circuit ELTN32-CORE.dig as structural Verilog
module ELTN32_CORE (
);

  wire _7404_3_pin11, _7408_3_pin3, _7408_3_pin6, _7408_3_pin8, _7408_3_pin10, _7408_6_pin3, _7408_6_pin6,
       _7432_3_pin9, _7432_3_pin10, _7432_3_pin12, _7432_3_pin13, _74193_1_pin14, BadState, BAND, EC0,
       EC0__SC0, EC0_SC0, EC0_SC0__plus__EC0__plus_SC0, EC0_t, EC1, EC1__SC1, EC1_SC1,
       EC1_SC1__plus__EC1__plus_SC1, EC1_t, EC2, EC2__SC2, EC2_SC2, EC2_SC2__plus__EC2__plus_SC2, EC2_t, EC3,
       EC3__SC3, EC3_SC3, EC3_SC3__plus__EC3__plus_SC3, EC3_t, EC4, EC4__SC4, EC4_SC4,
       EC4_SC4__plus__EC4__plus_SC4, EC4_t, EC5, EC5__SC5, EC5_SC5, EC5_SC5__plus__E51__plus_SC5, EC5_t, EC6,
       EC6__SC6, EC6_SC6, EC6_SC6__plus__EC6__plus_SC6, EC6_t, EC7, EC7__SC7, EC7_SC7,
       EC7_SC7__plus__EC7__plus_SC7, EC7_t, EnterBtn, GAND, IS5, IsLocked, IsMatch, not_1_out, not_2_out,
       not_3_out, notconnected_2_out, notconnected_3_out, or_1_out, QA, QB, QC, ResetBtn, SC0, SC0_t, SC1,
       SC1_t, SC2, SC2_t, SC3, SC3_t, SC4, SC4_t, SC5, SC5_t, SC6, SC6_t, SC7, SC7_t, UnlockState;
  wire [3:0] CountVal;

  Button ENTER (.out(EnterBtn));
  Button RESET (.out(ResetBtn));
  DipSwitch #(.Bits(8)) u_EC1 (.out(EC0));
  DipSwitch u_EC2 (.out(EC1));
  DipSwitch u_EC3 (.out(EC2));
  DipSwitch u_EC4 (.out(EC3));
  DipSwitch u_EC5 (.out(EC4));
  DipSwitch u_EC6 (.out(EC5));
  DipSwitch u_EC7 (.out(EC6));
  DipSwitch EC8 (.out(EC7));
  DipSwitch #(.Bits(8)) u_SC1 (.out(SC0));
  DipSwitch u_SC2 (.out(SC1));
  DipSwitch u_SC3 (.out(SC2));
  DipSwitch u_SC4 (.out(SC3));
  DipSwitch u_SC5 (.out(SC4));
  DipSwitch u_SC6 (.out(SC5));
  DipSwitch u_SC7 (.out(SC6));
  DipSwitch SC8 (.out(SC7));
  Seven_Seg_Hex seven_seg_hex_1 (.d(CountVal), .dp(1'b1));
  _7404 _7404_1 (
    .pin1(EC0), .pin2(EC0_t), .pin3(EC1), .pin4(EC1_t), .pin5(EC2), .pin6(EC2_t), .pin7(1'b0), .pin8(EC3_t),
    .pin9(EC3), .pin10(EC4_t), .pin11(EC4), .pin12(EC5_t), .pin13(EC5), .pin14(1'b1));
  _7404 _7404_2 (
    .pin1(EC6), .pin2(EC6_t), .pin3(EC7), .pin4(EC7_t), .pin5(SC0), .pin6(SC0_t), .pin7(1'b0), .pin8(SC1_t),
    .pin9(SC1), .pin10(SC2_t), .pin11(SC2), .pin12(SC3_t), .pin13(SC3), .pin14(1'b1));
  _7404 _7404_3 (
    .pin1(SC4), .pin2(SC4_t), .pin3(SC5), .pin4(SC5_t), .pin5(SC6), .pin6(SC6_t), .pin7(1'b0),
    .pin8(IsLocked), .pin9(IS5), .pin11(_7404_3_pin11), .pin12(SC7_t), .pin13(SC7), .pin14(1'b1));  // open: pin10
  LED UNLOCKED (.in(GAND));
  LED BAD_CODE (.in(BAND));
  LED LOCKED_OUT (.in(IsLocked));
  // NotConnected on _7404_3_pin11
  _7408 _7408_1 (
    .pin1(EC0), .pin2(SC0), .pin3(EC0_SC0), .pin4(SC0_t), .pin5(EC0_t), .pin6(EC0__SC0), .pin7(1'b0),
    .pin8(EC1__SC1), .pin9(SC1_t), .pin10(EC1_t), .pin11(EC1_SC1), .pin12(SC1), .pin13(EC1), .pin14(1'b1));
  _7408 _7408_2 (
    .pin1(EC4), .pin2(SC4), .pin3(EC4_SC4), .pin4(SC4_t), .pin5(EC4_t), .pin6(EC4__SC4), .pin7(1'b0),
    .pin8(EC5__SC5), .pin9(SC5_t), .pin10(EC5_t), .pin11(EC5_SC5), .pin12(SC5), .pin13(EC5), .pin14(1'b1));
  _7408 _7408_3 (
    .pin1(EC0_SC0__plus__EC0__plus_SC0), .pin2(EC1_SC1__plus__EC1__plus_SC1), .pin3(_7408_3_pin3),
    .pin4(_7408_3_pin3), .pin5(EC2_SC2__plus__EC2__plus_SC2), .pin6(_7408_3_pin6), .pin7(1'b0),
    .pin8(_7408_3_pin8), .pin9(EC4_SC4__plus__EC4__plus_SC4), .pin10(_7408_3_pin10), .pin11(_7408_3_pin10),
    .pin12(EC3_SC3__plus__EC3__plus_SC3), .pin13(_7408_3_pin6), .pin14(1'b1));
  _7408 _7408_4 (
    .pin1(EC2), .pin2(SC2), .pin3(EC2_SC2), .pin4(SC2_t), .pin5(EC2_t), .pin6(EC2__SC2), .pin7(1'b0),
    .pin8(EC3__SC3), .pin9(SC3_t), .pin10(EC3_t), .pin11(EC3_SC3), .pin12(SC3), .pin13(EC3), .pin14(1'b1));
  _7408 _7408_5 (
    .pin1(EC6), .pin2(SC6), .pin3(EC6_SC6), .pin4(SC6_t), .pin5(EC6_t), .pin6(EC6__SC6), .pin7(1'b0),
    .pin8(EC7__SC7), .pin9(SC7_t), .pin10(EC7_t), .pin11(EC7_SC7), .pin12(SC7), .pin13(EC7), .pin14(1'b1));
  _7408 _7408_6 (
    .pin1(_7408_3_pin8), .pin2(EC5_SC5__plus__E51__plus_SC5), .pin3(_7408_6_pin3), .pin4(_7408_6_pin3),
    .pin5(EC6_SC6__plus__EC6__plus_SC6), .pin6(_7408_6_pin6), .pin7(1'b0), .pin8(1'b0), .pin9(1'b0),
    .pin10(1'b0), .pin11(IsMatch), .pin12(EC7_SC7__plus__EC7__plus_SC7), .pin13(_7408_6_pin6), .pin14(1'b1));
  _7432 _7432_1 (
    .pin1(EC0_SC0), .pin2(EC0__SC0), .pin3(EC0_SC0__plus__EC0__plus_SC0), .pin4(EC1_SC1), .pin5(EC1__SC1),
    .pin6(EC1_SC1__plus__EC1__plus_SC1), .pin7(1'b0), .pin8(EC3_SC3__plus__EC3__plus_SC3), .pin9(EC3__SC3),
    .pin10(EC3_SC3), .pin11(EC2_SC2__plus__EC2__plus_SC2), .pin12(EC2__SC2), .pin13(EC2_SC2), .pin14(1'b1));
  _7432 _7432_2 (
    .pin1(EC4_SC4), .pin2(EC4__SC4), .pin3(EC4_SC4__plus__EC4__plus_SC4), .pin4(EC5_SC5), .pin5(EC5__SC5),
    .pin6(EC5_SC5__plus__E51__plus_SC5), .pin7(1'b0), .pin8(EC7_SC7__plus__EC7__plus_SC7), .pin9(EC7__SC7),
    .pin10(EC7_SC7), .pin11(EC6_SC6__plus__EC6__plus_SC6), .pin12(EC6__SC6), .pin13(EC6_SC6), .pin14(1'b1));
  _7442 _7442_1 (
    .pin6(IS5), .pin8(1'b0), .pin12(1'b0), .pin13(QC), .pin14(QB), .pin15(QA), .pin16(1'b1));  // open: pin1, pin2, pin3, pin4, pin5, pin7, pin9, pin10, pin11
  or or_1 (or_1_out, BAND, ResetBtn);
  _74193 _74193_1 (
    .pin1(1'b0), .pin2(QB), .pin3(QA), .pin4(1'b1), .pin5(BAND), .pin6(QC), .pin8(1'b0), .pin9(1'b0),
    .pin10(1'b0), .pin11(1'b1), .pin14(_74193_1_pin14), .pin15(1'b0), .pin16(1'b1));  // open: pin7, pin12, pin13
  Counter #(.Bits(4)) counter_1 (.en(1'b1), .C(or_1_out), .clr(ResetBtn), .out(CountVal));  // open: ovf
  not not_1 (not_1_out, IsMatch);
  // NotConnected on notconnected_2_out
  // NotConnected on notconnected_3_out
  not not_2 (not_2_out, IsLocked);
  not not_3 (not_3_out, IsLocked);
  _7432 _7432_3 (
    .pin1(ResetBtn), .pin2(GAND), .pin3(_74193_1_pin14), .pin4(notconnected_2_out),
    .pin5(notconnected_3_out), .pin7(1'b0), .pin9(_7432_3_pin9), .pin10(_7432_3_pin10),
    .pin12(_7432_3_pin12), .pin13(_7432_3_pin13), .pin14(1'b1));  // open: pin6, pin8, pin11
  and and_1 (BAND, EnterBtn, not_1_out, not_2_out);
  and and_2 (GAND, EnterBtn, IsMatch, not_3_out);
  // NotConnected on _7432_3_pin13
  // NotConnected on _7432_3_pin12
  // NotConnected on _7432_3_pin10
  // NotConnected on _7432_3_pin9
  RS_FF GoodLatch (.S(GAND), .C(1'b1), .R(ResetBtn), .Q(UnlockState));  // open: nQ
  RS_FF BadLatch (.S(BAND), .C(1'b1), .R(ResetBtn), .Q(BadState));  // open: nQ

  // Notes on the sheet:
  //   ENTRY CODE (EC)
  //   SECRET CODE (SC)
  //   7404
  //   Hex Inverter
  //   EC0-EC5
  //   7404
  //   Hex Inverter
  //   EC6-EC7
  //   SC1-SC3
  //   7404
  //   Hex Inverter
  //   SC4-SC7
  //   7408 - AND 
  //   EC0 & SC0, EC0' & SC0'
  //   EC1 & SC1, EC1' & SC1'
  //   7408 - AND
  //   EC4 & SC4, EC4' & SC4'
  //   EC5 & SC5, EC5' & SC5'
  //   IsMatch
  //   2X 7408 AND 
  //   (EC0&SC0)+(EC0'+SC0') & (EC1&SC1)+(EC1'+SC1') & 
  //   (EC2&SC2)+(EC2'+SC2') & (EC3&SC3)+(EC3'+SC3') & 
  //   (EC4&SC4)+(EC4'+SC4') & (EC5&SC5)+(E51'+SC5') & 
  //   (EC6&SC6)+(EC6'+SC6') & (EC7&SC7)+(EC7'+SC7')
  //   7408 - AND
  //   EC2 & SC2, EC2' & SC2'
  //   EC3 & SC3, EC3' & SC3'
  //   7408 - AND
  //   EC6 & SC6, EC6' & SC6'
  //   EC7 & SC7, EC7' & SC7'
  //   7432 Quad 2 Input OR
  //   (EC0&SC0)+(EC0'+SC0')
  //   (EC1&SC1)+(EC1'+SC1')
  //   (EC2&SC2)+(EC2'+SC2')
  //   (EC3&SC3)+(EC3'+SC3')
  //   7432 Quad 2 Input OR
  //   (EC4&SC4)+(EC4'+SC4')
  //   (EC5&SC5)+(E51'+SC5')
  //   (EC6&SC6)+(EC6'+SC6')
  //   (EC7&SC7)+(EC7'+SC7')
  //   7442 (BCD to Decimal Decoder)
  //   74193 (4-bit Up/Down Counter)
  //   7432 Quad 2 Input OR
endmodule
